# Fritzing sketch ultrasonicRange (saved by Fritzing 0.9.3b)
breadboards: 1

parts:
  BeagleBone1 = BeagleBone Black
  SONAR1 = Maxbotix MaxSonar Ultrasonic Sensor

nets:
  N1: BeagleBone1.no_name_yet#1, SONAR1.GND
  N2: BeagleBone1.no_name_yet#3, SONAR1.+5V
  N3: BeagleBone1.no_name_yet#40, SONAR1.AN

notes:
  +
  -

custom parts:
  BeagleBone Black: BeagleBone Black rev. A5B
  Maxbotix MaxSonar Ultrasonic Sensor: Maxbotix MaxSonar Ultrasonic Sensor LV-EZ0, LV-EZ1, LV-EZ2, LV-EZ3, LV-EZ4
